# Fritzing sketch PicupGlasses (saved by Fritzing 0.9.3b)

parts:
  Gesture_Sensor_-_APDS-9960 = Triple Axis Magnetometer - HMC5883 Breakout
  3_7v_Lithium_Battery = LIPO-1000mAh [package=lipo-1000]
  HC-06_Blue_Tooth_Module = Bluetooth HC-05 Macho
  U1 = TCM8240MD [package=tcm8240md]
  U2 = SUP500F [package=sup500f]  # not connected
  부품1 = Power Cell LiPo Charger/Booster
  0_49_Inch_OLED_Display = Grove OLED 128x96
  부품2 = Arduino Pro Mini (3.3V)

nets:
  GND: Gesture_Sensor_-_APDS-9960.GND, HC-06_Blue_Tooth_Module.GND, 0_49_Inch_OLED_Display.GND, 부품2.GND
  VCC: Gesture_Sensor_-_APDS-9960.VCC, HC-06_Blue_Tooth_Module.VCC, 0_49_Inch_OLED_Display.VCC, 부품2.VCC
  N1: Gesture_Sensor_-_APDS-9960.SDA, 0_49_Inch_OLED_Display.SDA, 부품2.A4
  N2: Gesture_Sensor_-_APDS-9960.SCL, 0_49_Inch_OLED_Display.SCL, 부품2.A5
  N3: 3_7v_Lithium_Battery.+, 부품1.5VIN
  GND_2: 3_7v_Lithium_Battery.-, U1.GND, 부품1.GND
  N4: HC-06_Blue_Tooth_Module.TXD, 부품2.D10
  N5: HC-06_Blue_Tooth_Module.RXD, 부품2.MOSI
  N6: U1.DOUT2, 부품2.MISO
  N7: U1.DVDD(1.6V), 부품1.VCC

notes:
  Gesture Sensor
  Mini Spy Camera
  SIG to pin 12
  All SDA's to
  A4.All
  SCL's to A5
  TP4056
